// Logisim project Processor(1).circ as structural Verilog: 16 circuits, main circuit ArithmeticUint
module ArithmeticUint (
  input  [31:0] in_1,
  input  [31:0] in_2,
  input  [1:0] in_3,
  output [31:0] out_4
);

  wire [31:0] adder_1_out, divider_1_out, shifter_1_out, subtractor_1_out;

  Adder #(.width(32)) adder_1 (.a(in_1), .b(in_2), .out(adder_1_out));  // open: cin, cout
  Subtractor #(.width(32)) subtractor_1 (.a(in_1), .b(in_2), .out(subtractor_1_out));  // open: bin, bout
  Divider #(.width(32)) divider_1 (.a(in_1), .b(in_2), .out(divider_1_out));  // open: upper, rem
  Shifter #(.width(32)) shifter_1 (.in(in_1), .\dist (in_2[4:0]), .out(shifter_1_out));
  Multiplexer #(.select(2), .width(32), .enable("false")) multiplexer_1 (
    .in0(adder_1_out), .in1(subtractor_1_out), .in2(shifter_1_out), .in3(divider_1_out), .out(out_4),
    .sel(in_3));
endmodule

module LogicalUnit (
  input  [31:0] in_1,
  input  [31:0] in_2,
  input  [1:0] in_3,
  output [31:0] out_4
);

  wire [31:0] and_1_out, nor_1_out, or_1_out, xor_1_out;

  assign and_1_out = in_1 & in_2;  // AND_Gate and_1, 32 bits wide
  assign or_1_out = in_1 | in_2;  // OR_Gate or_1, 32 bits wide
  assign nor_1_out = ~(in_1 | in_2);  // NOR_Gate nor_1, 32 bits wide
  assign xor_1_out = in_1 ^ in_2;  // XOR_Gate xor_1, 32 bits wide
  Multiplexer #(.select(2), .width(32), .enable("false")) multiplexer_1 (
    .in0(and_1_out), .in1(or_1_out), .in2(nor_1_out), .in3(xor_1_out), .out(out_4), .sel(in_3));
endmodule

module ALU (
  input  [31:0] in_1,
  input  [31:0] in_2,
  input  [2:0] in_3,
  output [31:0] out_4
);

  wire [31:0] arithmeticuint_1_out_4, logicalunit_1_out_4;

  LogicalUnit logicalunit_1 (.in_1(in_1), .in_2(in_2), .in_3(in_3[1:0]), .out_4(logicalunit_1_out_4));
  ArithmeticUint arithmeticuint_1 (.in_1(in_1), .in_2(in_2), .in_3(in_3[1:0]), .out_4(arithmeticuint_1_out_4));
  Multiplexer #(.width(32), .enable("false")) multiplexer_1 (
    .in0(logicalunit_1_out_4), .in1(arithmeticuint_1_out_4), .out(out_4), .sel(in_3[2]));
endmodule

module SR (
  input  R,
  input  S,
  output out_3
);

  wire nor_1_out;

  nor nor_1 (nor_1_out, out_3, S);
  nor nor_2 (out_3, R, nor_1_out);
endmodule

module DLatch (
  input  C,
  input  D,
  output out_3
);

  wire and_1_out, and_2_out, not_1_out;

  not not_1 (not_1_out, D);
  and and_1 (and_1_out, C, not_1_out);
  and and_2 (and_2_out, C, D);
  SR sr_1 (.R(and_1_out), .S(and_2_out), .out_3(out_3));

  // Notes on the sheet:
  //   D latch
  //   When C=0,no output changes
  //   When C=1,output changes as input D changes
endmodule

module D_FF (
  input  C,
  input  D,
  output Q
);

  wire dlatch_1_out_3, not_1_out;

  not not_1 (not_1_out, C);
  DLatch dlatch_1 (.C(not_1_out), .D(D), .out_3(dlatch_1_out_3));
  DLatch dlatch_2 (.C(C), .D(dlatch_1_out_3), .out_3(Q));

  // Notes on the sheet:
  //   Master - Slave D Flipflop
  //   D Latch
  //   D Latch
endmodule

module register (
  input  C,
  input  load,
  input  D,
  output Q
);

  wire and_1_out;

  and and_1 (and_1_out, C, load);
  D_FF d_ff_1 (.C(and_1_out), .D(D), .Q(Q));

  // Notes on the sheet:
  //   D FlipFlop
endmodule

module registerFile (
  input  [31:0] in_1,
  input  write_enable,
  input  [1:0] write_address,
  input  [1:0] A_addr,
  input  [1:0] B_addr,
  input  clock,
  output [31:0] A,
  output [31:0] B
);

  wire demultiplexer_1_out0, demultiplexer_1_out1, demultiplexer_1_out2, demultiplexer_1_out3;
  wire [31:0] register_1_q, register_2_q, register_3_q, register_4_q;

  Demultiplexer #(.select(2), .enable("false")) demultiplexer_1 (
    .out0(demultiplexer_1_out0), .out1(demultiplexer_1_out1), .out2(demultiplexer_1_out2),
    .out3(demultiplexer_1_out3), .in(write_enable), .sel(write_address));
  Register #(.width(32)) register_1 (.D(in_1), .en(demultiplexer_1_out0), .clk(clock), .Q(register_1_q));  // open: clr
  Register #(.width(32)) register_2 (.D(in_1), .en(demultiplexer_1_out1), .clk(clock), .Q(register_2_q));  // open: clr
  Register #(.width(32)) register_3 (.D(in_1), .en(demultiplexer_1_out2), .clk(clock), .Q(register_3_q));  // open: clr
  Register #(.width(32)) register_4 (.D(in_1), .en(demultiplexer_1_out3), .clk(clock), .Q(register_4_q));  // open: clr
  Multiplexer #(.select(2), .width(32), .enable("false")) multiplexer_1 (
    .in0(register_1_q), .in1(register_2_q), .in2(register_3_q), .in3(register_4_q), .out(A), .sel(A_addr));
  Multiplexer #(.select(2), .width(32), .enable("false")) multiplexer_2 (
    .in0(register_1_q), .in1(register_2_q), .in2(register_3_q), .in3(register_4_q), .out(B), .sel(B_addr));

  // Notes on the sheet:
  //   add $1,$2,$3
  //   sw $1,0($2)
endmodule

module RAMTest (
  input  [7:0] in_1,
  input  in_2,
  input  in_3,
  input  [31:0] in_4,
  output [31:0] out_5
);

  RAM #(.dataWidth(32), .databus("bibus")) ram_1 (
    .addr(in_1), .we(in_2), .clk(in_3), .din(in_4), .dout(out_5));  // open: oe
endmodule

module RomTest (
  input  [7:0] in_1,
  output [31:0] out_2
);

  ROM #(.dataWidth(32)) rom_1 (.addr(in_1), .data(out_2));
endmodule

module instructionfetch (
  input  in_1,
  input  CLK,
  input  Reset,
  input  beq,
  input  zero,
  input  [31:0] imm,
  output [31:0] out_7
);

  wire and_1_out;
  wire [4:0] undriven;
  wire [31:0] adder_1_out, adder_2_out, multiplexer_1_out, register_1_q, shifter_1_out;

  Register #(.width(32)) register_1 (.D(multiplexer_1_out), .en(in_1), .clk(CLK), .Q(register_1_q), .clr(Reset));
  Adder #(.width(32)) adder_1 (.a(32'h4), .b(register_1_q), .out(adder_1_out));  // open: cin, cout
  and and_1 (and_1_out, beq, zero);
  Shifter #(.width(32)) shifter_1 (.in(imm), .\dist (undriven), .out(shifter_1_out));
  Adder #(.width(32)) adder_2 (.a(adder_1_out), .b(shifter_1_out), .out(adder_2_out), .cout(and_1_out));  // open: cin
  ROM #(.dataWidth(32)) rom_1 (.addr(register_1_q[9:2]), .data(out_7));
  Multiplexer #(.width(32), .enable("false")) multiplexer_1 (
    .in0(adder_1_out), .in1(adder_2_out), .out(multiplexer_1_out));  // open: sel
endmodule

module MIPSProcessor (
  input  in_1,
  input  in_2,
  input  in_3,
  output [31:0] out_4,
  output [31:0] out_5
);

  wire [31:0] instructionfetch_1_out_7;

  instructionfetch instructionfetch_1 (
    .CLK(in_1), .Reset(in_2), .beq(in_3), .out_7(instructionfetch_1_out_7));  // open: in_1, zero, imm
  InstructionDecode instructiondecode_1 (
    .instr(instructionfetch_1_out_7), .out_4(out_4), .out_5(out_5));  // open: CLK, C
endmodule

// ID
module InstructionDecode (
  input  [31:0] instr,
  input  CLK,
  input  [31:0] C,
  output [31:0] out_4,
  output [31:0] out_5
);

  wire [1:0] undriven;
  wire [31:0] undriven_4, undriven_5, undriven_6, undriven_7;
  wire [31:1] undriven_2, undriven_3;

  Multiplexer #(.enable("false")) multiplexer_1 ();  // open: in0, in1, out, sel
  // RegisterFile32 registerfile32_1: pin names not known; wires that end beside it: C, CLK, instr[31:21], instr[20:16], out_4, out_5
  // OR_Gate or_1 has open pins: in0={undriven_2, undriven[0]}, in1={undriven_3, undriven[1]}, in2=undriven_4, in3=undriven_5, in4=undriven_6, in5=undriven_7, out=open
  // Pins of 1 and 32 bits meet at {undriven_2, undriven[0]}
  // Pins of 1 and 32 bits meet at {undriven_3, undriven[1]}
endmodule

module RegisterFile16 (
  input  [31:0] in_1,
  input  write_enable,
  input  [3:0] write_address,
  input  clock,
  input  [3:0] A_addr,
  input  [3:0] B_addr,
  output [31:0] A,
  output [31:0] B
);

  wire demultiplexer_1_out0, demultiplexer_1_out1, demultiplexer_1_out2, demultiplexer_1_out3;
  wire [31:0] registerfile4_1_a, registerfile4_1_b, registerfile4_2_a, registerfile4_2_b, registerfile4_3_a,
       registerfile4_3_b, registerfile4_4_a, registerfile4_4_b;

  Demultiplexer #(.select(2), .enable("false")) demultiplexer_1 (
    .out0(demultiplexer_1_out0), .out1(demultiplexer_1_out1), .out2(demultiplexer_1_out2),
    .out3(demultiplexer_1_out3), .in(write_enable), .sel(write_address[3:2]));
  RegisterFile4 registerfile4_1 (
    .in_1(in_1), .write_enable(demultiplexer_1_out0), .write_address(write_address[1:0]), .clock(clock),
    .A_addr(A_addr[1:0]), .B_addr(B_addr[1:0]), .A(registerfile4_1_a), .B(registerfile4_1_b));
  RegisterFile4 registerfile4_2 (
    .in_1(in_1), .write_enable(demultiplexer_1_out1), .write_address(write_address[1:0]), .clock(clock),
    .A_addr(A_addr[1:0]), .B_addr(B_addr[1:0]), .A(registerfile4_2_a), .B(registerfile4_2_b));
  RegisterFile4 registerfile4_3 (
    .in_1(in_1), .write_enable(demultiplexer_1_out2), .write_address(write_address[1:0]), .clock(clock),
    .A_addr(A_addr[1:0]), .B_addr(B_addr[1:0]), .A(registerfile4_3_a), .B(registerfile4_3_b));
  RegisterFile4 registerfile4_4 (
    .in_1(in_1), .write_enable(demultiplexer_1_out3), .write_address(write_address[1:0]), .clock(clock),
    .A_addr(A_addr[1:0]), .B_addr(B_addr[1:0]), .A(registerfile4_4_a), .B(registerfile4_4_b));
  Multiplexer #(.select(2), .width(32), .enable("false")) multiplexer_1 (
    .in0(registerfile4_1_b), .in1(registerfile4_2_b), .in2(registerfile4_3_b), .in3(registerfile4_4_b),
    .out(B), .sel(B_addr[3:2]));
  Multiplexer #(.select(2), .width(32), .enable("false")) multiplexer_2 (
    .in0(registerfile4_1_a), .in1(registerfile4_2_a), .in2(registerfile4_3_a), .in3(registerfile4_4_a),
    .out(A), .sel(A_addr[3:2]));

  // Notes on the sheet:
  //   add $1,$2,$3
  //   sw $1,0($2)
endmodule

module RegisterFile4 (
  input  [31:0] in_1,
  input  write_enable,
  input  [1:0] write_address,
  input  clock,
  input  [1:0] A_addr,
  input  [1:0] B_addr,
  output [31:0] A,
  output [31:0] B
);

  wire demultiplexer_1_out0, demultiplexer_1_out1, demultiplexer_1_out2, demultiplexer_1_out3;
  wire [31:0] register_1_q, register_2_q, register_3_q, register_4_q;

  Demultiplexer #(.select(2), .enable("false")) demultiplexer_1 (
    .out0(demultiplexer_1_out0), .out1(demultiplexer_1_out1), .out2(demultiplexer_1_out2),
    .out3(demultiplexer_1_out3), .in(write_enable), .sel(write_address));
  Register #(.width(32)) register_1 (.D(in_1), .en(demultiplexer_1_out0), .clk(clock), .Q(register_1_q));  // open: clr
  Register #(.width(32)) register_2 (.D(in_1), .en(demultiplexer_1_out1), .clk(clock), .Q(register_2_q));  // open: clr
  Register #(.width(32)) register_3 (.D(in_1), .en(demultiplexer_1_out2), .clk(clock), .Q(register_3_q));  // open: clr
  Register #(.width(32)) register_4 (.D(in_1), .en(demultiplexer_1_out3), .clk(clock), .Q(register_4_q));  // open: clr
  Multiplexer #(.select(2), .width(32), .enable("false")) multiplexer_1 (
    .in0(register_1_q), .in1(register_2_q), .in2(register_3_q), .in3(register_4_q), .out(B), .sel(B_addr));
  Multiplexer #(.select(2), .width(32), .enable("false")) multiplexer_2 (
    .in0(register_1_q), .in1(register_2_q), .in2(register_3_q), .in3(register_4_q), .out(A), .sel(A_addr));

  // Notes on the sheet:
  //   add $1,$2,$3
  //   sw $1,0($2)
endmodule

module RegisterFile32 (
  input  [31:0] in_1,
  input  write_enable,
  input  [4:0] write_address,
  input  clock,
  input  [4:0] A_addr,
  input  [4:0] B_addr,
  output [31:0] A,
  output [31:0] B
);

  wire demultiplexer_1_out0, demultiplexer_1_out1;
  wire [31:0] registerfile16_1_a, registerfile16_1_b, registerfile16_2_a, registerfile16_2_b;

  Demultiplexer #(.enable("false")) demultiplexer_1 (
    .out0(demultiplexer_1_out0), .out1(demultiplexer_1_out1), .in(write_enable), .sel(write_address[4]));
  RegisterFile16 registerfile16_1 (
    .in_1(in_1), .write_enable(demultiplexer_1_out0), .write_address(write_address[3:0]), .clock(clock),
    .A_addr(A_addr[3:0]), .B_addr(B_addr[3:0]), .A(registerfile16_1_a), .B(registerfile16_1_b));
  RegisterFile16 registerfile16_2 (
    .in_1(in_1), .write_enable(demultiplexer_1_out1), .write_address(write_address[3:0]), .clock(clock),
    .A_addr(A_addr[3:0]), .B_addr(B_addr[3:0]), .A(registerfile16_2_a), .B(registerfile16_2_b));
  Multiplexer #(.width(32), .enable("false")) multiplexer_1 (
    .in0(registerfile16_1_b), .in1(registerfile16_2_b), .out(B), .sel(B_addr[4]));
  Multiplexer #(.width(32), .enable("false")) multiplexer_2 (
    .in0(registerfile16_1_a), .in1(registerfile16_2_a), .out(A), .sel(A_addr[4]));

  // Notes on the sheet:
  //   add $1,$2,$3
  //   sw $1,0($2)
endmodule
